# Fritzing sketch 02-d-logic-gate (saved by Fritzing 0.9.10b)
circuit board: 8.46667cm x 5.64444cm
breadboards: 2

parts:
  S1 = Momentary Switch [package=ksa_sealed_tac_switch]
  XTAL1 = Crystal [frequency="16 Mhz" package=THT]
  C1_22pF = Capacitor [package=cap-pth-small2]
  C2_22pF = Capacitor [package=cap-pth-small2]
  LED2 = LED - 3mm [color="Blue (505nm)" current=0.030 package="3 mm [THT]"]
  C3_1uF = Capacitor Polarized [package=cpol-radial-10uf-25v]
  USB_UART = FTDI Basic Programmer
  U2 = atmega328 [package=dip]
  R2 = Resistor [tolerance=±5% resistance=10k power=0.25 package=THT]
  R1 = Resistor [tolerance=±5% resistance=10k power=0.25 package=THT]
  LED3 = LED - 5mm [color="Red (633nm)" current=0.030 package="5 mm [THT]"]
  R3 = Resistor [tolerance=±5% resistance=220 package="0402 [SMD]"]
  S2 = Pushbutton [package="[SMD]"]
  R4 = Resistor [tolerance=±5% resistance=10k package="0402 [SMD]"]
  S3 = Pushbutton [package="[SMD]"]
  S4 = Pushbutton [package="[SMD]"]
  R5 = Resistor [tolerance=±5% resistance=10k package="0402 [SMD]"]
  R6 = Resistor [tolerance=±5% resistance=10k package="0402 [SMD]"]
  LED4 = LED - 5mm [color="Red (633nm)" current=0.030 package="5 mm [THT]"]
  LED5 = LED - 5mm [color="Red (633nm)" current=0.030 package="5 mm [THT]"]
  R7 = Resistor [tolerance=±5% resistance=220 package="0402 [SMD]"]
  R8 = Resistor [tolerance=±5% resistance=220 package="0402 [SMD]"]

nets:
  N1: S1.2, C3_1uF.-, U2.RESET, R2.Pin_0
  GND: S1.4, C1_22pF.2, C2_22pF.1, LED2.cathode, USB_UART.GND, U2.GND, R3.Pin_1, R4.Pin_1, R5.Pin_1, R6.Pin_1, R7.Pin_1, R8.Pin_1
  N2: XTAL1.pin_0, C2_22pF.2, U2.XLAT1
  N3: XTAL1.pin_1, C1_22pF.1, U2.XLAT2
  N4: LED2.anode, R1.Pin_1
  N5: C3_1uF.+, USB_UART.DTR
  N6: USB_UART.RXI, U2.D1_(TX)
  N7: USB_UART.TXO, U2.D0_(RX)
  N8: USB_UART.POWER, U2.VCC, U2.AVCC, R2.Pin_1
  N9: U2.D5_(PWM), S2.Pin_3, S2.Pin_4, R4.Pin_0
  N10: U2.D6_(PWM), S3.Pin_3, S3.Pin_4, R5.Pin_0
  N11: U2.D7, S4.Pin_3, S4.Pin_4, R6.Pin_0
  N12: U2.D9_(PWM), LED3.anode
  N13: U2.D10_(PWM), LED4.anode
  N14: U2.D11_(PWM), LED5.anode
  N15: U2.D13, R1.Pin_0
  N16: LED3.cathode, R3.Pin_0
  N17: S2.Pin_1, S2.Pin_2, S3.Pin_1, S3.Pin_2, S4.Pin_1, S4.Pin_2
  N18: LED4.cathode, R7.Pin_0
  N19: LED5.cathode, R8.Pin_0
