# Fritzing sketch 04-eeprom (saved by Fritzing 0.9.10b)
circuit board: 8.46667cm x 5.64444cm
breadboards: 2

parts:
  S1 = Momentary Switch [package=ksa_sealed_tac_switch]
  XTAL1 = Crystal [frequency="16 Mhz" package=THT]
  C1_22pF = Capacitor [package=cap-pth-small2]
  C2_22pF = Capacitor [package=cap-pth-small2]
  LED2 = LED - 3mm [color="Blue (505nm)" current=0.030 package="3 mm [THT]"]
  C3_1uF = Capacitor Polarized [package=cpol-radial-10uf-25v]
  USB_UART = FTDI Basic Programmer
  U2 = atmega328 [package=dip]
  R2 = Resistor [tolerance=±5% resistance=10k power=0.25 package=THT]
  R1 = Resistor [tolerance=±5% resistance=10k power=0.25 package=THT]
  LED3 = LED - 5mm [color="Red (633nm)" current=0.030 package="5 mm [THT]"]
  R3 = Resistor [tolerance=±5% resistance=220 package="0402 [SMD]"]
  S2 = Pushbutton [package="[SMD]"]
  R4 = Resistor [tolerance=±5% resistance=10k package="0402 [SMD]"]

nets:
  N1: S1.2, C3_1uF.-, U2.RESET, R2.Pin_0
  GND: S1.4, C1_22pF.2, C2_22pF.1, LED2.cathode, USB_UART.GND, U2.GND, R3.Pin_1, R4.Pin_1
  N2: XTAL1.pin_0, C2_22pF.2, U2.XLAT1
  N3: XTAL1.pin_1, C1_22pF.1, U2.XLAT2
  N4: LED2.anode, R1.Pin_1
  N5: C3_1uF.+, USB_UART.DTR
  N6: USB_UART.RXI, U2.D1_(TX)
  N7: USB_UART.TXO, U2.D0_(RX)
  N8: USB_UART.POWER, U2.VCC, U2.AVCC, R2.Pin_1
  N9: U2.D5_(PWM), S2.Pin_3, S2.Pin_4, R4.Pin_0
  N10: U2.D9_(PWM), LED3.anode
  N11: U2.D13, R1.Pin_0
  N12: LED3.cathode, R3.Pin_0
  N13: S2.Pin_1, S2.Pin_2
